// Logisim project cpu.circ as structural Verilog: 1 circuit, main circuit cpu
module cpu (
  input  clk,
  input  [31:0] INSTRUCTION,
  input  [31:0] READ_DATA,
  output [31:0] WRITE_ADDRESS,
  output [31:0] PROGRAM_COUNTER,
  output [31:0] ra,
  output [31:0] sp,
  output [31:0] t0,
  output [31:0] t1,
  output [31:0] t2,
  output [31:0] s0,
  output [31:0] s1,
  output [31:0] a0,
  output [31:0] tohost,
  output [3:0] WRITE_ENABLE,
  output [31:0] WRITE_DATA
);

  wire BSel, RegWEn;
  wire [2:0] ImmSel;
  wire [3:0] ALUSel;
  wire [31:0] A, adder_1_out, ALUResult, B, imm, INST, RD2;

  Adder #(.width(32)) adder_1 (.a(PROGRAM_COUNTER), .b(32'h4), .out(adder_1_out));  // open: cin, cout
  Register #(.width(32)) PC (.D(adder_1_out), .clk(clk), .Q(PROGRAM_COUNTER));  // open: en, clr
  Register #(.width(32)) register_1 (.D(INSTRUCTION), .clk(clk), .Q(INST));  // open: en, clr
  control_logic control_logic_1 (
    .RegWEn(RegWEn), .ImmSel(ImmSel), .BSel(BSel), .ALUSel(ALUSel));  // open: CSRWen, PCSel, BrUn, ASel, MemRW, WBSel, CSRSel, inst, BrEq, BrLt
  imm_gen imm_gen_1 (.inst(INST), .ImmSel(ImmSel), .imm(imm));
  regfile regfile_1 (
    .rs1(INST[19:15]), .rs2(INST[24:20]), .rd(INST[11:7]), .Write_Data(ALUResult), .RegWEn(RegWEn),
    .clk(clk), .ra(ra), .sp(sp), .t0(t0), .t1(t1), .t2(t2), .s0(s0), .s1(s1), .a0(a0), .Read_Data_1(A),
    .Read_Data_2(RD2));
  // branch_comp branch_comp_1: pin names not known
  Multiplexer #(.enable("false"), .width(32)) multiplexer_1 (.in0(RD2), .in1(imm), .out(B), .sel(BSel));
  // csr csr_1: pin names not known; wires that end beside it: tohost
  alu alu_1 (.Result(ALUResult), .A(A), .B(B), .ALUSel(ALUSel));

  // Other names for the same wires on the sheet: rd[4:0] = INST[11:7]; rs1[4:0] = INST[19:15]; rs2[4:0] = INST[24:20];
  //   RD1[31:0] = A

  // Notes on the sheet:
  //   Output to IMEM
  //   IMEM (do **NOT** move this)
  //   Inputs from IMEM
  //   原INSTRUCTION解码部分，更改为左下角寄存器
  //   改为流水线后imm_gen的输入需要改为流水线寄存器的输出值来控制时钟周期
  //   It is OK to move the PC, RegFile, ALU, MEM, Branch Comp, Imm Gen, and Control Logic to wherever is most convenient for you when constructing your CPU, and to delete this text
  //   Inputs/Outputs for testing. Do **NOT** move these.
  //   Outputs To DMEM
  //   DMEM (do **NOT** move this)
  //   Inputs From DMEM
endmodule
