// Logisim project ex1_test.circ as structural Verilog: 1 circuit, main circuit main
module main (
  output [7:0] out_1,
  output NAND_OUT,
  output NOR_OUT,
  output XOR_OUT,
  output halt,
  output MUX2_OUT,
  output MUX4_OUT,
  output out_8,
  output out_9,
  output out_10,
  output out_11,
  output out_12,
  output out_13
);

  wire clock_1_out;
  wire [7:0] adder_1_out;

  Clock clock_1 (.out(clock_1_out));
  Adder adder_1 (.a(8'h1), .b(out_1), .out(adder_1_out));  // open: cin, cout
  Register register_1 (.D(adder_1_out), .clk(clock_1_out), .Q(out_1));  // open: en, clr
  ROM #(.dataWidth(1)) rom_1 (.addr(out_1));  // open: data
  ROM #(.dataWidth(1)) rom_2 (.addr(out_1));  // open: data
  ROM #(.dataWidth(1)) rom_3 ();  // open: addr, data
  Comparator comparator_1 (.a(out_1), .b(8'h7), .eq(halt));  // open: gt, lt
  ROM #(.dataWidth(1)) rom_4 (.addr(out_1));  // open: data
  ROM #(.dataWidth(1)) rom_5 (.addr(out_1));  // open: data
  NAND1 nand1_1 (.A(out_8), .B(out_9), .RESULT(NAND_OUT));
  NOR1 nor1_1 (.A(out_8), .B(out_9), .RESULT(NOR_OUT));
  XOR1 xor1_1 (.A(out_8), .B(out_9), .RESULT(XOR_OUT));
  MUX2 mux2_1 (.A(out_8), .B(out_9), .Sel(out_12), .RESULT(MUX2_OUT));
  MUX4 mux4_1 (.A(out_8), .B(out_9), .C(out_10), .D(out_11), .Sel1(out_12), .Sel2(out_13), .RESULT(MUX4_OUT));
  ROM #(.dataWidth(1)) rom_6 (.addr(out_1));  // open: data
  ROM #(.dataWidth(1)) rom_7 (.addr(out_1));  // open: data

  // Other names for the same wires on the sheet: A = out_8; B = out_9; C = out_10; D = out_11; Sel1 = out_12;
  //   Sel2 = out_13; Test[7:0] = out_1

  // Notes on the sheet:
  //   contents of rom_1 (hex, n*v repeats v):
  //   0 0 1 1
  //   contents of rom_2 (hex, n*v repeats v):
  //   0 0 1 1
  //   contents of rom_4 (hex, n*v repeats v):
  //   0 1 0 1
  //   contents of rom_5 (hex, n*v repeats v):
  //   0 1 0 1
  //   contents of rom_6 (hex, n*v repeats v):
  //   1 0 1 1
  //   contents of rom_7 (hex, n*v repeats v):
  //   0 1 1
endmodule
